// Logisim project 7segmentp2.circ as structural Verilog: 2 circuits, main circuit main
module main (
  input  w,
  input  x,
  input  y,
  input  z
);

  wire and_1_out, and_2_out, and_3_out, and_4_out, and_5_out, and_6_out, and_7_out, and_8_out, and_9_out,
       and_10_out, and_11_out, not_1_out, not_2_out, not_3_out, not_4_out, or_1_out, or_2_out, or_3_out,
       or_4_out, or_5_out, or_6_out;

  not not_1 (not_1_out, w);
  not not_2 (not_2_out, x);
  not not_3 (not_3_out, y);
  not not_4 (not_4_out, z);
  and and_1 (and_1_out, x, not_3_out, not_4_out);
  and and_2 (and_2_out, not_1_out, not_2_out, not_3_out, z);
  and and_3 (and_3_out, x, not_3_out, z);
  and and_4 (and_4_out, x, y, not_4_out);
  and and_5 (and_5_out, not_2_out, y, not_4_out);
  and and_6 (and_6_out, x, y, z);
  and and_7 (and_7_out, x, not_3_out);
  and and_8 (and_8_out, y, z);
  and and_9 (and_9_out, not_2_out, y);
  and and_10 (and_10_out, not_1_out, not_2_out, z);
  and and_11 (and_11_out, not_1_out, not_2_out, not_3_out);
  or or_1 (or_1_out, and_1_out, and_2_out);
  or or_2 (or_2_out, and_3_out, and_4_out);
  or or_3 (or_3_out, and_1_out, and_6_out, and_2_out);
  or or_4 (or_4_out, z, and_7_out);
  or or_5 (or_5_out, and_8_out, and_9_out, and_10_out);
  or or_6 (or_6_out, and_6_out, and_11_out);
  _7_Segment_Display #(.active("false")) u_7_segment_display_1 (
    .g(or_6_out), .f(or_5_out), .a(or_1_out), .b(or_2_out), .e(or_4_out), .d(or_3_out), .c(and_5_out));  // open: dp
endmodule

module main2 (
  input  w,
  input  x,
  input  y,
  input  z
);

  wire nand_1_out, nand_2_out, nand_3_out, nand_4_out, nand_5_out, nand_7_out, nand_8_out, nand_10_out,
       nand_11_out, nand_12_out, nand_13_out, nand_14_out, nand_15_out, nand_16_out, nor_1_out, not_1_out,
       not_2_out, not_3_out, not_4_out;

  not not_1 (not_1_out, w);
  not not_2 (not_2_out, x);
  not not_3 (not_3_out, y);
  not not_4 (not_4_out, z);
  nand nand_1 (nand_1_out, x, not_3_out, not_4_out);
  nand nand_2 (nand_2_out, not_1_out, not_2_out, not_3_out, z);
  nand nand_3 (nand_3_out, x, not_3_out, z);
  nand nand_4 (nand_4_out, x, y, not_4_out);
  nor nor_1 (nor_1_out, x, not_3_out, z);
  nand nand_5 (nand_5_out, x, y, z);
  // NAND_Gate nand_6 has open pins: in0=x, in1=not_3_out, out=open
  nand nand_7 (nand_7_out, y, z);
  nand nand_8 (nand_8_out, not_2_out, y);
  // NAND_Gate nand_9 has open pins: in0=not_1_out, in1=not_2_out, in2=z, out=open
  nand nand_10 (nand_10_out, not_1_out, not_2_out, not_3_out);
  nand nand_11 (nand_11_out, nand_1_out, nand_2_out);
  nand nand_12 (nand_12_out, nand_3_out, nand_4_out);
  nand nand_13 (nand_13_out, nand_2_out, nand_5_out, nand_1_out);
  nand nand_14 (nand_14_out, nand_1_out, not_4_out);
  nand nand_15 (nand_15_out, nand_7_out, nand_2_out, nand_8_out);
  nand nand_16 (nand_16_out, nand_5_out, nand_10_out);
  _7_Segment_Display #(.active("false")) u_7_segment_display_1 (
    .g(nand_16_out), .f(nand_15_out), .a(nand_11_out), .b(nand_12_out), .e(nand_14_out), .d(nand_13_out),
    .c(nor_1_out));  // open: dp

  // Notes on the sheet:
  //   X
  //   X
endmodule
