// Logisim project improvedLalloc.circ as structural Verilog: 11 circuits, main circuit overflow
module main (
  input  RST,
  output [15:0] CycleCount
);

  wire AS, CLK, decode_1_sub, HLT, I, Jmp, JmpNeg, Load, meminterface_1_pow, Move, NegRes, not_1_out,
       Operation, programcounter_1_clkout, programcounter_1_high, programcounter_1_low, register_1_q, Store,
       undriven, undriven_2, writeback_1_clk1, writeback_1_clk1_2, writeback_1_clk3, writeback_1_clk3_2,
       writeback_1_rst2, writeback_1_rst2_2, writeback_1_rst4, writeback_1_rst4_2, writeback_1_we1,
       writeback_1_we2, writeback_1_we3, writeback_1_we4;
  wire [1:0] LDI, Rd;
  wire [5:0] JmpDat, programcounter_1_count;
  wire [7:0] EXE, INST, Instruction_dout, meminterface_1_ldrg, WB;
  wire [15:0] adder_1_out, adder_2_out, DataIn, DataOut, FinalResult, LoadReg, R0, R1, R2, R3, register_4_q,
       register_5_q, register_6_q, register_7_q, RSLT, sourcesplit_1_a, sourcesplit_1_b, subtractor_1_out,
       undriven_3, writeback_1_out1, writeback_1_out2, writeback_1_out3, writeback_1_out4;

  Clock u_CLK (.out(CLK));
  sourceSplit sourcesplit_1 (
    .R0(R0), .R1(R1), .R2(R2), .R3(R3), .Rd(Rd), .Rs(LDI), .A2(DataIn), .B2(LoadReg), .A(sourcesplit_1_a),
    .B(sourcesplit_1_b));
  Adder #(.width(16)) adder_1 (.a(sourcesplit_1_a), .b(sourcesplit_1_b), .out(adder_1_out));  // open: cin, cout
  Subtractor #(.width(16)) subtractor_1 (
    .a(sourcesplit_1_a), .b(sourcesplit_1_b), .out(subtractor_1_out));  // open: bin, bout
  resultMux resultmux_1 (
    .DataOut(DataOut), .LDI({{14{1'b0}}, LDI}), .ALU(RSLT), .LoadReg(LoadReg), .I(I), .AS(AS), .Move(Move),
    .Load(Load), .FinalResult(FinalResult), .NegativeResult(NegRes));
  Register #(.width(1)) register_1 (.D(1'b1), .en(HLT), .clk(CLK), .Q(register_1_q), .clr(RST));
  decode decode_1 (
    .instruction(INST), .CLK(CLK), .NegativeResult(NegRes), .RST(RST), .rd(Rd), .rs(LDI), .hlt(HLT),
    .jd(JmpDat), .st(Store), .mv(Move), .load(Load), .ldi(I), .sub(decode_1_sub), .JumpNegative(JmpNeg),
    .AS(AS), .jmp(Jmp), .Operation(Operation));
  Multiplexer #(.width(16)) multiplexer_1 (.in0(adder_1_out), .in1(subtractor_1_out), .out(RSLT), .sel(decode_1_sub));
  not not_1 (not_1_out, register_1_q);
  Register #(.width(16)) register_2 (.D(adder_2_out), .en(not_1_out), .clk(CLK), .Q(CycleCount), .clr(RST));
  Adder #(.width(16)) adder_2 (.a(CycleCount), .b(16'h1), .out(adder_2_out));  // open: cin, cout
  RAM #(.asyncread("true"), .dataWidth(16), .trigger("falling")) Data (
    .addr(meminterface_1_ldrg), .we(undriven), .oe(meminterface_1_pow), .clk(undriven_2), .din(undriven_3),
    .dout(DataOut));
  memInterface meminterface_1 (
    .LoadReg(LoadReg), .Clock({Store, undriven}), .Store({CLK, undriven_2}),
    .DataIn({DataIn[15], undriven_3[15], DataIn[14], undriven_3[14], DataIn[13], undriven_3[13], DataIn[12], undriven_3[12], DataIn[11], undriven_3[11], DataIn[10], undriven_3[10], DataIn[9], undriven_3[9], DataIn[8], undriven_3[8], DataIn[7], undriven_3[7], DataIn[6], undriven_3[6], DataIn[5], undriven_3[5], DataIn[4], undriven_3[4], DataIn[3], undriven_3[3], DataIn[2], undriven_3[2], DataIn[1], undriven_3[1], DataIn[0], undriven_3[0]}),
    .ldrg(meminterface_1_ldrg), .pow(meminterface_1_pow));
  RAM #(.addrWidth(6), .asyncread("true"), .trigger("falling")) Instruction (
    .addr(programcounter_1_count), .we(programcounter_1_low), .oe(programcounter_1_high),
    .clk(programcounter_1_clkout), .dout(Instruction_dout));  // open: din
  programCounter programcounter_1 (
    .JumpFlag(Jmp), .JumpNegativeFlag(JmpNeg), .JumpData(JmpDat), .clk(CLK), .rst(RST),
    .count(programcounter_1_count), .clkout(programcounter_1_clkout), .Low(programcounter_1_low),
    .High(programcounter_1_high));
  Register register_3 (.D(Instruction_dout), .en(1'b1), .clk(CLK), .Q(INST), .clr(RST));
  Register #(.width(16)) register_4 (
    .D(writeback_1_out1), .en(writeback_1_we1), .clk(writeback_1_clk1), .Q(register_4_q),
    .clr(writeback_1_rst2));
  Register #(.width(16)) register_5 (
    .D(writeback_1_out2), .en(writeback_1_we2), .clk(writeback_1_clk1_2), .Q(register_5_q),
    .clr(writeback_1_rst2_2));
  Register #(.width(16)) register_6 (
    .D(writeback_1_out3), .en(writeback_1_we3), .clk(writeback_1_clk3), .Q(register_6_q),
    .clr(writeback_1_rst4));
  Register #(.width(16)) register_7 (
    .D(writeback_1_out4), .en(writeback_1_we4), .clk(writeback_1_clk3_2), .Q(register_7_q),
    .clr(writeback_1_rst4_2));
  Register register_8 (.D(INST), .en(1'b1), .clk(CLK), .Q(EXE), .clr(RST));
  writeBack writeback_1 (
    .Operation(Operation),
    .F2({register_5_q[15], R1[15], register_5_q[14], R1[14], register_5_q[13], R1[13], register_5_q[12], R1[12], register_5_q[11], R1[11], register_5_q[10], R1[10], register_5_q[9], R1[9], register_5_q[8], R1[8], register_5_q[7], R1[7], register_5_q[6], R1[6], register_5_q[5], R1[5], register_5_q[4], R1[4], register_5_q[3], R1[3], register_5_q[2], R1[2], register_5_q[1], R1[1], register_5_q[0], R1[0]}),
    .F3({register_6_q[15], R2[15], register_6_q[14], R2[14], register_6_q[13], R2[13], register_6_q[12], R2[12], register_6_q[11], R2[11], register_6_q[10], R2[10], register_6_q[9], R2[9], register_6_q[8], R2[8], register_6_q[7], R2[7], register_6_q[6], R2[6], register_6_q[5], R2[5], register_6_q[4], R2[4], register_6_q[3], R2[3], register_6_q[2], R2[2], register_6_q[1], R2[1], register_6_q[0], R2[0]}),
    .F4({register_7_q[15], R3[15], register_7_q[14], R3[14], register_7_q[13], R3[13], register_7_q[12], R3[12], register_7_q[11], R3[11], register_7_q[10], R3[10], register_7_q[9], R3[9], register_7_q[8], R3[8], register_7_q[7], R3[7], register_7_q[6], R3[6], register_7_q[5], R3[5], register_7_q[4], R3[4], register_7_q[3], R3[3], register_7_q[2], R3[2], register_7_q[1], R3[1], register_7_q[0], R3[0]}),
    .Rd(Rd),
    .FO1({register_4_q[15], R0[15], register_4_q[14], R0[14], register_4_q[13], R0[13], register_4_q[12], R0[12], register_4_q[11], R0[11], register_4_q[10], R0[10], register_4_q[9], R0[9], register_4_q[8], R0[8], register_4_q[7], R0[7], register_4_q[6], R0[6], register_4_q[5], R0[5], register_4_q[4], R0[4], register_4_q[3], R0[3], register_4_q[2], R0[2], register_4_q[1], R0[1], register_4_q[0], R0[0]}),
    .FinalResult(FinalResult), .Reset(RST), .Clk1({CLK, writeback_1_clk1, writeback_1_clk1_2}),
    .Out1(writeback_1_out1), .We1(writeback_1_we1), .Out2(writeback_1_out2), .We2(writeback_1_we2),
    .Out3(writeback_1_out3), .We3(writeback_1_we3), .Out4(writeback_1_out4), .We4(writeback_1_we4),
    .Clk3({writeback_1_clk3, writeback_1_clk3_2}), .Rst2({writeback_1_rst2, writeback_1_rst2_2}),
    .Rst4({writeback_1_rst4, writeback_1_rst4_2}));
  Register register_9 (.D(EXE), .en(1'b1), .clk(CLK), .Q(WB), .clr(RST));

  // Other names for the same wires on the sheet: Rs[1:0] = LDI
endmodule

module overflow (
  input  AddSub,
  input  OV,
  input  Clock,
  input  Reset,
  output Q
);

  wire and_1_out;

  and and_1 (and_1_out, AddSub, OV);
  Register #(.width(1)) Ovfl (.D(1'b1), .en(and_1_out), .clk(Clock), .Q(Q), .clr(Reset));
endmodule

module writeBack (
  input  [15:0] F1,
  input  Clock,
  input  [15:0] F2,
  input  [15:0] F3,
  input  [15:0] F4,
  input  Reset,
  input  [15:0] FinalResult,
  input  [1:0] Rd,
  input  Operation,
  output [15:0] FO1,
  output Clk2,
  output Clk1,
  output Clk4,
  output Clk3,
  output [15:0] FO2,
  output [15:0] FO3,
  output Rst1,
  output Rst2,
  output Rst3,
  output Rst4,
  output [15:0] FO4,
  output [15:0] Out1,
  output We1,
  output [15:0] Out2,
  output We2,
  output [15:0] Out3,
  output We3,
  output [15:0] Out4,
  output We4
);

  regWE regwe_1 (.Rd(Rd), .regWrite(Operation), .reg0(We1), .reg1(We2), .reg2(We3), .reg3(We4));

  assign Clk1 = Clock;
  assign Clk2 = Clock;
  assign Clk3 = Clock;
  assign Clk4 = Clock;
  assign FO1 = F1;
  assign FO2 = F2;
  assign FO3 = F3;
  assign FO4 = F4;
  assign Out1 = FinalResult;
  assign Out2 = FinalResult;
  assign Out3 = FinalResult;
  assign Out4 = FinalResult;
  assign Rst1 = Reset;
  assign Rst2 = Reset;
  assign Rst3 = Reset;
  assign Rst4 = Reset;
endmodule

module pipeline (
  input  [7:0] InstructionOut,
  input  Reset,
  input  Clock,
  output [7:0] Instruction,
  output [7:0] Execute,
  output [7:0] WriteBack
);

  Register register_1 (.D(InstructionOut), .en(1'b1), .clk(Clock), .Q(Instruction), .clr(Reset));
  Register register_2 (.D(Instruction), .en(1'b1), .clk(Clock), .Q(Execute), .clr(Reset));
  Register register_3 (.D(Execute), .en(1'b1), .clk(Clock), .Q(WriteBack), .clr(Reset));
endmodule

module resultMux (
  input  [15:0] DataOut,
  input  [15:0] LDI,
  input  I,
  input  AS,
  input  Load,
  input  [15:0] ALU,
  input  Move,
  input  [15:0] LoadReg,
  output NegativeResult,
  output [15:0] FinalResult
);

  wire or_1_out;
  wire [15:0] multiplexer_1_out, multiplexer_2_out;

  Multiplexer #(.width(16)) multiplexer_1 (.in0(DataOut), .in1(LDI), .out(multiplexer_1_out), .sel(I));
  Multiplexer #(.width(16)) multiplexer_2 (.in0(multiplexer_1_out), .in1(ALU), .out(multiplexer_2_out), .sel(AS));
  and and_1 (NegativeResult, or_1_out, FinalResult[15]);
  or or_1 (or_1_out, AS, I, Move, Load);
  Multiplexer #(.width(16)) multiplexer_3 (.in0(multiplexer_2_out), .in1(LoadReg), .out(FinalResult), .sel(Move));
endmodule

module sourceSplit (
  input  [1:0] Rd,
  input  [1:0] Rs,
  input  [15:0] R0,
  input  [15:0] R1,
  input  [15:0] R2,
  input  [15:0] R3,
  output [15:0] A2,
  output [15:0] A,
  output [15:0] B2,
  output [15:0] B
);

  srcSel srcsel_1 (.R0(R0), .R1(R1), .R2(R2), .R3(R3), .Sel(Rd), .Q(A));
  srcSel srcsel_2 (.R0(R0), .R1(R1), .R2(R2), .R3(R3), .Sel(Rs), .Q(B));

  assign A2 = A;
  assign B2 = B;
endmodule

module memInterface (
  input  [15:0] LoadReg,
  input  Clock,
  input  Store,
  input  [15:0] DataIn,
  output [7:0] ldrg,
  output clk,
  output pow,
  output st,
  output [15:0] di
);


  assign clk = Clock;
  assign di = DataIn;
  assign ldrg = LoadReg[7:0];
  assign pow = 1'b1;
  assign st = Store;
endmodule

module srcSel (
  input  [15:0] R0,
  input  [15:0] R1,
  input  [15:0] R2,
  input  [15:0] R3,
  input  [1:0] Sel,
  output [15:0] Q
);

  wire [15:0] multiplexer_1_out, multiplexer_2_out;

  Multiplexer #(.width(16)) multiplexer_1 (.in0(R0), .in1(R1), .out(multiplexer_1_out), .sel(Sel[0]));
  Multiplexer #(.width(16)) multiplexer_2 (.in0(R2), .in1(R3), .out(multiplexer_2_out), .sel(Sel[0]));
  Multiplexer #(.width(16)) multiplexer_3 (.in0(multiplexer_1_out), .in1(multiplexer_2_out), .out(Q), .sel(Sel[1]));
endmodule

module decode (
  input  NegativeResult,
  input  [7:0] instruction,
  input  RST,
  input  CLK,
  output JumpNegative,
  output hlt,
  output jmp,
  output [5:0] jd,
  output st,
  output mv,
  output ldi,
  output load,
  output Operation,
  output AS,
  output sub,
  output [1:0] rd,
  output [1:0] rs
);

  wire and_1_out, and_2_out, and_3_out, and_4_out, and_5_out, and_6_out, and_7_out, and_8_out, and_9_out,
       and_10_out, d_ff_1_q, not_1_out, not_2_out, not_3_out, not_4_out, not_5_out, not_6_out, not_7_out,
       not_8_out, not_9_out, register_6_q;

  and and_1 (and_1_out, instruction[4], instruction[5], instruction[6], instruction[7]);
  not not_1 (not_1_out, instruction[2]);
  not not_2 (not_2_out, instruction[3]);
  not not_3 (not_3_out, instruction[1]);
  not not_4 (not_4_out, instruction[0]);
  not not_5 (not_5_out, instruction[1]);
  not not_6 (not_6_out, instruction[2]);
  not not_7 (not_7_out, instruction[0]);
  not not_8 (not_8_out, instruction[3]);
  not not_9 (not_9_out, instruction[0]);
  and and_2 (and_2_out, not_3_out, instruction[0]);
  and and_3 (and_3_out, and_1_out, and_6_out);
  and and_4 (and_4_out, not_4_out, not_5_out);
  and and_5 (and_5_out, instruction[0], instruction[1], not_6_out, instruction[3]);
  and and_6 (and_6_out, not_7_out, instruction[1], instruction[2], not_8_out);
  and and_7 (and_7_out, instruction[3], instruction[2], instruction[1], not_9_out);
  and and_8 (and_8_out, instruction[3], instruction[2], instruction[1], instruction[0]);
  and and_9 (and_9_out, not_9_out, instruction[1], not_2_out, not_1_out);
  and and_10 (and_10_out, instruction[0], instruction[1], not_1_out, not_2_out);
  Register #(.width(1)) register_1 (.D(and_3_out), .clk(CLK), .Q(hlt), .clr(RST));  // open: en
  Register #(.width(1)) register_2 (.D(and_5_out), .clk(CLK), .Q(st), .clr(RST));  // open: en
  Register #(.width(1)) register_3 (.D(and_6_out), .clk(CLK), .Q(mv), .clr(RST));  // open: en
  Register #(.width(1)) register_4 (.D(and_7_out), .clk(CLK), .Q(ldi), .clr(RST));  // open: en
  Register #(.width(1)) register_5 (.D(and_8_out), .clk(CLK), .Q(load), .clr(RST));  // open: en
  Register #(.width(1)) register_6 (.D(and_9_out), .clk(CLK), .Q(register_6_q), .clr(RST));  // open: en
  Register #(.width(1)) register_7 (.D(and_10_out), .clk(CLK), .Q(sub), .clr(RST));  // open: en
  Register #(.width(2)) register_8 (.D(instruction[7:6]), .clk(CLK), .Q(rd), .clr(RST));  // open: en
  Register #(.width(2)) register_9 (.D(instruction[5:4]), .clk(CLK), .Q(rs), .clr(RST));  // open: en
  and and_11 (JumpNegative, and_2_out, NegativeResult);
  D_Flip_Flop d_ff_1 (.D(1'b1), .clk(CLK), .Q(d_ff_1_q), .reset(RST));  // open: Qn, preset
  or or_1 (AS, register_6_q, sub);
  or or_2 (Operation, mv, load, ldi, AS);
  and and_12 (jmp, and_4_out, d_ff_1_q);

  assign jd = instruction[7:2];
endmodule

module regWE (
  input  [1:0] Rd,
  input  regWrite,
  output reg0,
  output reg1,
  output reg2,
  output reg3
);

  wire not_1_out, not_2_out;

  not not_1 (not_1_out, Rd[1]);
  not not_2 (not_2_out, Rd[0]);
  and and_1 (reg0, not_1_out, not_2_out, regWrite);
  and and_2 (reg1, Rd[0], not_1_out, regWrite);
  and and_3 (reg2, Rd[1], not_2_out, regWrite);
  and and_4 (reg3, Rd[1], Rd[0], regWrite);
endmodule

module programCounter (
  input  [5:0] JumpData,
  input  clk,
  input  JumpFlag,
  input  rst,
  input  JumpNegativeFlag,
  output [5:0] count,
  output Low,
  output High,
  output clkout
);

  wire or_1_out;
  wire [5:0] adder_1_out, multiplexer_1_out;

  Adder #(.width(6)) adder_1 (.a(count), .b(6'b000001), .out(adder_1_out));  // open: cin, cout
  or or_1 (or_1_out, JumpFlag, JumpNegativeFlag);
  Multiplexer #(.width(6)) multiplexer_1 (.in0(adder_1_out), .in1(JumpData), .out(multiplexer_1_out), .sel(or_1_out));
  Register #(.width(6)) register_1 (.D(multiplexer_1_out), .en(1'b1), .clk(clk), .Q(count), .clr(rst));

  assign clkout = clk;
  assign High = 1'b1;
  assign Low = 1'b0;
endmodule
