// Logisim project onetwothree.circ as structural Verilog: 2 circuits, main circuit main
module main (
  input  in_1,
  input  in_2
);

  wire nand_1_out, nand_2_out, nor_1_out, not_1_out, not_2_out;

  not not_1 (not_1_out, in_1);
  not not_2 (not_2_out, in_2);
  nand nand_1 (nand_1_out, not_1_out, in_2);
  nand nand_2 (nand_2_out, in_1, not_2_out);
  nor nor_1 (nor_1_out, in_1, in_2);
  _7_Segment_Display u_7_segment_display_1 (
    .g(in_1), .f(nor_1_out), .a(nand_1_out), .b(1'b1), .e(not_2_out), .d(nand_1_out), .c(nand_2_out));  // open: dp
endmodule

module main2 (
  input  A,
  input  B
);

  wire Inverter_pin2, Inverter_pin4, NAND1_pin3, NAND1_pin6, NOR1_p2;

  _7404 Inverter (
    .pin1(A), .pin2(Inverter_pin2), .pin3(B), .pin4(Inverter_pin4));  // open: pin5, pin6, pin13, pin12, pin11, pin10, pin9, pin8
  _7400 NAND1 (
    .pin1(Inverter_pin2), .pin2(B), .pin3(NAND1_pin3), .pin4(A), .pin5(Inverter_pin4), .pin6(NAND1_pin6));  // open: pin13, pin12, pin11, pin10, pin9, pin8
  // _7402 NOR1: pin names not known; wires that end beside it: 1'b1, NOR1_p2, A, B, 1'b0
  _7_Segment_Display u_7_segment_display_1 (
    .g(A), .f(NOR1_p2), .a(NAND1_pin3), .b(1'b1), .e(Inverter_pin4), .d(NAND1_pin3), .c(NAND1_pin6));  // open: dp
endmodule
