// Logisim project umwhatisit.circ as structural Verilog: 43 circuits, main circuit main
module main (
  input  RST,
  output [15:0] CycleCount
);

  wire AS, CLK, decode_1_sub, HLT, I, Jmp, JmpNeg, Load, meminterface_1_clk, meminterface_1_pow,
       meminterface_1_st, Move, NegRes, Operation, overflow_1_q, Ovfl, programcounter_1_clkout,
       programcounter_1_high, programcounter_1_low, Store, writeback_1_clk2, writeback_1_clk2_2,
       writeback_1_clk4, writeback_1_clk4_2, writeback_1_rst1, writeback_1_rst1_2, writeback_1_rst3,
       writeback_1_rst3_2, writeback_1_we1, writeback_1_we2, writeback_1_we3, writeback_1_we4;
  wire [1:0] LDI, Rd;
  wire [5:0] JmpDat, programcounter_1_count;
  wire [7:0] EXE, INST, Instruction_dout, meminterface_1_ldrg, WB;
  wire [15:0] DataIn, DataOut, FinalResult, LoadReg, meminterface_1_di, R0, R1, R2, R3, register_1_q,
       register_2_q, register_3_q, register_4_q, RSLT, sourcesplit_1_a, sourcesplit_1_b, writeback_1_out1,
       writeback_1_out2, writeback_1_out3, writeback_1_out4;

  Clock u_CLK (.out(CLK));
  sourceSplit sourcesplit_1 (
    .R0(R0), .R1(R1), .R2(R2), .R3(R3), .Rd(Rd), .Rs(LDI), .A2(DataIn), .B2(LoadReg), .A(sourcesplit_1_a),
    .B(sourcesplit_1_b));
  resultMux resultmux_1 (
    .DataOut(DataOut), .LDI({{14{1'b0}}, LDI}), .ALU(RSLT), .LoadReg(LoadReg), .I(I), .AS(AS), .Move(Move),
    .Load(Load), .FinalResult(FinalResult), .NegativeResult(NegRes));
  decode decode_1 (
    .instruction(INST), .CLK(CLK), .NegativeResult(NegRes), .RST(RST), .rd(Rd), .rs(LDI), .hlt(HLT),
    .jd(JmpDat), .st(Store), .mv(Move), .load(Load), .ldi(I), .sub(decode_1_sub), .JumpNegative(JmpNeg),
    .AS(AS), .jmp(Jmp), .Operation(Operation));
  finalAdder finaladder_1 (.a(sourcesplit_1_a), .b(sourcesplit_1_b), .opp(decode_1_sub), .sum(RSLT), .ovfl(Ovfl));
  cycleCounter cyclecounter_1 (.Halt(HLT), .Clock(CLK), .Reset(RST), .count(CycleCount));
  RAM #(.asyncread("true"), .dataWidth(16), .trigger("falling")) Data (
    .addr(meminterface_1_ldrg), .we(meminterface_1_clk), .oe(meminterface_1_pow), .clk(meminterface_1_st),
    .din(meminterface_1_di), .dout(DataOut));
  memInterface meminterface_1 (
    .LoadReg(LoadReg), .clk({Store, meminterface_1_clk}), .st({CLK, meminterface_1_st}),
    .di({DataIn[15], meminterface_1_di[15], DataIn[14], meminterface_1_di[14], DataIn[13], meminterface_1_di[13], DataIn[12], meminterface_1_di[12], DataIn[11], meminterface_1_di[11], DataIn[10], meminterface_1_di[10], DataIn[9], meminterface_1_di[9], DataIn[8], meminterface_1_di[8], DataIn[7], meminterface_1_di[7], DataIn[6], meminterface_1_di[6], DataIn[5], meminterface_1_di[5], DataIn[4], meminterface_1_di[4], DataIn[3], meminterface_1_di[3], DataIn[2], meminterface_1_di[2], DataIn[1], meminterface_1_di[1], DataIn[0], meminterface_1_di[0]}),
    .ldrg(meminterface_1_ldrg), .pow(meminterface_1_pow));
  RAM #(.addrWidth(6), .asyncread("true"), .trigger("falling")) Instruction (
    .addr(programcounter_1_count), .we(programcounter_1_low), .oe(programcounter_1_high),
    .clk(programcounter_1_clkout), .dout(Instruction_dout));  // open: din
  programCounter programcounter_1 (
    .JumpFlag(Jmp), .JumpNegativeFlag(JmpNeg), .JumpData(JmpDat), .clk(CLK), .rst(RST),
    .count(programcounter_1_count), .clkout(programcounter_1_clkout), .Low(programcounter_1_low),
    .High(programcounter_1_high));
  pipeline pipeline_1 (
    .InstructionOut(Instruction_dout), .Reset(RST), .Clock(CLK), .Instruction(INST), .Execute(EXE),
    .WriteBack(WB));
  overflow overflow_1 (.AddSub(AS), .OV(Ovfl), .Clock(CLK), .Reset(RST), .Q(overflow_1_q));
  LED led_1 (.in(overflow_1_q));
  Register #(.width(16)) register_1 (
    .D(writeback_1_out1), .en(writeback_1_we1), .clk(writeback_1_clk2), .Q(register_1_q),
    .clr(writeback_1_rst1));
  Register #(.width(16)) register_2 (
    .D(writeback_1_out2), .en(writeback_1_we2), .clk(writeback_1_clk2_2), .Q(register_2_q),
    .clr(writeback_1_rst1_2));
  Register #(.width(16)) register_3 (
    .D(writeback_1_out3), .en(writeback_1_we3), .clk(writeback_1_clk4), .Q(register_3_q),
    .clr(writeback_1_rst3));
  Register #(.width(16)) register_4 (
    .D(writeback_1_out4), .en(writeback_1_we4), .clk(writeback_1_clk4_2), .Q(register_4_q),
    .clr(writeback_1_rst3_2));
  writeBack writeback_1 (
    .Operation(Operation),
    .FO2({register_2_q[15], R1[15], register_2_q[14], R1[14], register_2_q[13], R1[13], register_2_q[12], R1[12], register_2_q[11], R1[11], register_2_q[10], R1[10], register_2_q[9], R1[9], register_2_q[8], R1[8], register_2_q[7], R1[7], register_2_q[6], R1[6], register_2_q[5], R1[5], register_2_q[4], R1[4], register_2_q[3], R1[3], register_2_q[2], R1[2], register_2_q[1], R1[1], register_2_q[0], R1[0]}),
    .FO3({register_3_q[15], R2[15], register_3_q[14], R2[14], register_3_q[13], R2[13], register_3_q[12], R2[12], register_3_q[11], R2[11], register_3_q[10], R2[10], register_3_q[9], R2[9], register_3_q[8], R2[8], register_3_q[7], R2[7], register_3_q[6], R2[6], register_3_q[5], R2[5], register_3_q[4], R2[4], register_3_q[3], R2[3], register_3_q[2], R2[2], register_3_q[1], R2[1], register_3_q[0], R2[0]}),
    .FO4({register_4_q[15], R3[15], register_4_q[14], R3[14], register_4_q[13], R3[13], register_4_q[12], R3[12], register_4_q[11], R3[11], register_4_q[10], R3[10], register_4_q[9], R3[9], register_4_q[8], R3[8], register_4_q[7], R3[7], register_4_q[6], R3[6], register_4_q[5], R3[5], register_4_q[4], R3[4], register_4_q[3], R3[3], register_4_q[2], R3[2], register_4_q[1], R3[1], register_4_q[0], R3[0]}),
    .Rd(Rd),
    .F1({register_1_q[15], R0[15], register_1_q[14], R0[14], register_1_q[13], R0[13], register_1_q[12], R0[12], register_1_q[11], R0[11], register_1_q[10], R0[10], register_1_q[9], R0[9], register_1_q[8], R0[8], register_1_q[7], R0[7], register_1_q[6], R0[6], register_1_q[5], R0[5], register_1_q[4], R0[4], register_1_q[3], R0[3], register_1_q[2], R0[2], register_1_q[1], R0[1], register_1_q[0], R0[0]}),
    .FinalResult(FinalResult), .Reset(RST), .Clk2({CLK, writeback_1_clk2, writeback_1_clk2_2}),
    .Out1(writeback_1_out1), .We1(writeback_1_we1), .Out2(writeback_1_out2), .We2(writeback_1_we2),
    .Out3(writeback_1_out3), .We3(writeback_1_we3), .Out4(writeback_1_out4), .We4(writeback_1_we4),
    .Clk4({writeback_1_clk4, writeback_1_clk4_2}), .Rst1({writeback_1_rst1, writeback_1_rst1_2}),
    .Rst3({writeback_1_rst3, writeback_1_rst3_2}));

  // Other names for the same wires on the sheet: Rs[1:0] = LDI
endmodule

module overflow (
  input  AddSub,
  input  OV,
  input  Clock,
  input  Reset,
  output Q
);

  wire and_1_out;

  and and_1 (and_1_out, AddSub, OV);
  Register #(.width(1)) Ovfl (.D(1'b1), .en(and_1_out), .clk(Clock), .Q(Q), .clr(Reset));
endmodule

module writeBack (
  input  [15:0] F1,
  input  Clock,
  input  [15:0] F2,
  input  [15:0] F3,
  input  [15:0] F4,
  input  Reset,
  input  [15:0] FinalResult,
  input  [1:0] Rd,
  input  Operation,
  output [15:0] FO1,
  output Clk1,
  output Clk2,
  output Clk3,
  output Clk4,
  output [15:0] FO2,
  output [15:0] FO3,
  output Rst2,
  output Rst1,
  output Rst4,
  output Rst3,
  output [15:0] FO4,
  output [15:0] Out1,
  output We1,
  output [15:0] Out2,
  output We2,
  output [15:0] Out3,
  output We3,
  output [15:0] Out4,
  output We4
);

  regWE regwe_1 (.Rd(Rd), .regWrite(Operation), .reg0(We1), .reg1(We2), .reg2(We3), .reg3(We4));

  assign Clk1 = Clock;
  assign Clk2 = Clock;
  assign Clk3 = Clock;
  assign Clk4 = Clock;
  assign FO1 = F1;
  assign FO2 = F2;
  assign FO3 = F3;
  assign FO4 = F4;
  assign Out1 = FinalResult;
  assign Out2 = FinalResult;
  assign Out3 = FinalResult;
  assign Out4 = FinalResult;
  assign Rst1 = Reset;
  assign Rst2 = Reset;
  assign Rst3 = Reset;
  assign Rst4 = Reset;
endmodule

module pipeline (
  input  [7:0] InstructionOut,
  input  Reset,
  input  Clock,
  output [7:0] Instruction,
  output [7:0] Execute,
  output [7:0] WriteBack
);

  Register register_1 (.D(InstructionOut), .en(1'b1), .clk(Clock), .Q(Instruction), .clr(Reset));
  Register register_2 (.D(Instruction), .en(1'b1), .clk(Clock), .Q(Execute), .clr(Reset));
  Register register_3 (.D(Execute), .en(1'b1), .clk(Clock), .Q(WriteBack), .clr(Reset));
endmodule

module resultMux (
  input  [15:0] DataOut,
  input  [15:0] LDI,
  input  I,
  input  AS,
  input  Load,
  input  [15:0] ALU,
  input  Move,
  input  [15:0] LoadReg,
  output NegativeResult,
  output [15:0] FinalResult
);

  wire or_1_out;
  wire [15:0] multiplexer_1_out, multiplexer_2_out;

  Multiplexer #(.width(16)) multiplexer_1 (.in0(DataOut), .in1(LDI), .out(multiplexer_1_out), .sel(I));
  Multiplexer #(.width(16)) multiplexer_2 (.in0(multiplexer_1_out), .in1(ALU), .out(multiplexer_2_out), .sel(AS));
  and and_1 (NegativeResult, or_1_out, FinalResult[15]);
  or or_1 (or_1_out, AS, I, Move, Load);
  Multiplexer #(.width(16)) multiplexer_3 (.in0(multiplexer_2_out), .in1(LoadReg), .out(FinalResult), .sel(Move));
endmodule

module cycleCounter (
  input  Halt,
  input  Clock,
  input  Reset,
  output [15:0] count
);

  wire not_1_out, register_1_q;
  wire [15:0] adder_1_out;

  Register #(.width(1)) register_1 (.D(1'b1), .en(Halt), .clk(Clock), .Q(register_1_q), .clr(Reset));
  Register #(.width(16)) register_2 (.D(adder_1_out), .en(not_1_out), .clk(Clock), .Q(count), .clr(Reset));
  Adder #(.width(16)) adder_1 (.a(count), .b(16'h1), .out(adder_1_out));  // open: cin, cout
  not not_1 (not_1_out, register_1_q);
endmodule

module sourceSplit (
  input  [1:0] Rd,
  input  [1:0] Rs,
  input  [15:0] R0,
  input  [15:0] R1,
  input  [15:0] R2,
  input  [15:0] R3,
  output [15:0] A2,
  output [15:0] A,
  output [15:0] B2,
  output [15:0] B
);

  srcSel srcsel_1 (.R0(R0), .R1(R1), .R2(R2), .R3(R3), .Sel(Rd), .Q(A));
  srcSel srcsel_2 (.R0(R0), .R1(R1), .R2(R2), .R3(R3), .Sel(Rs), .Q(B));

  assign A2 = A;
  assign B2 = B;
endmodule

module memInterface (
  input  [15:0] LoadReg,
  input  Clock,
  input  Store,
  input  [15:0] DataIn,
  output [7:0] ldrg,
  output clk,
  output pow,
  output st,
  output [15:0] di
);


  assign clk = Clock;
  assign di = DataIn;
  assign ldrg = LoadReg[7:0];
  assign pow = 1'b1;
  assign st = Store;
endmodule

module srcSel (
  input  [15:0] R0,
  input  [15:0] R1,
  input  [15:0] R2,
  input  [15:0] R3,
  input  [1:0] Sel,
  output [15:0] Q
);

  wire [15:0] multiplexer_1_out, multiplexer_2_out;

  Multiplexer #(.width(16)) multiplexer_1 (.in0(R0), .in1(R1), .out(multiplexer_1_out), .sel(Sel[0]));
  Multiplexer #(.width(16)) multiplexer_2 (.in0(R2), .in1(R3), .out(multiplexer_2_out), .sel(Sel[0]));
  Multiplexer #(.width(16)) multiplexer_3 (.in0(multiplexer_1_out), .in1(multiplexer_2_out), .out(Q), .sel(Sel[1]));
endmodule

module decode (
  input  NegativeResult,
  input  [7:0] instruction,
  input  RST,
  input  CLK,
  output JumpNegative,
  output hlt,
  output jmp,
  output [5:0] jd,
  output st,
  output mv,
  output ldi,
  output load,
  output Operation,
  output AS,
  output sub,
  output [1:0] rd,
  output [1:0] rs
);

  wire and_1_out, and_2_out, and_3_out, and_4_out, and_5_out, and_6_out, and_7_out, and_8_out, and_9_out,
       and_10_out, d_ff_1_q, not_1_out, not_2_out, not_3_out, not_4_out, not_5_out, not_6_out, not_7_out,
       not_8_out, not_9_out, register_6_q;

  and and_1 (and_1_out, instruction[4], instruction[5], instruction[6], instruction[7]);
  not not_1 (not_1_out, instruction[2]);
  not not_2 (not_2_out, instruction[3]);
  not not_3 (not_3_out, instruction[1]);
  not not_4 (not_4_out, instruction[0]);
  not not_5 (not_5_out, instruction[1]);
  not not_6 (not_6_out, instruction[2]);
  not not_7 (not_7_out, instruction[0]);
  not not_8 (not_8_out, instruction[3]);
  not not_9 (not_9_out, instruction[0]);
  and and_2 (and_2_out, not_3_out, instruction[0]);
  and and_3 (and_3_out, and_1_out, and_6_out);
  and and_4 (and_4_out, not_4_out, not_5_out);
  and and_5 (and_5_out, instruction[0], instruction[1], not_6_out, instruction[3]);
  and and_6 (and_6_out, not_7_out, instruction[1], instruction[2], not_8_out);
  and and_7 (and_7_out, instruction[3], instruction[2], instruction[1], not_9_out);
  and and_8 (and_8_out, instruction[3], instruction[2], instruction[1], instruction[0]);
  and and_9 (and_9_out, not_9_out, instruction[1], not_2_out, not_1_out);
  and and_10 (and_10_out, instruction[0], instruction[1], not_1_out, not_2_out);
  Register #(.width(1)) register_1 (.D(and_3_out), .clk(CLK), .Q(hlt), .clr(RST));  // open: en
  Register #(.width(1)) register_2 (.D(and_5_out), .clk(CLK), .Q(st), .clr(RST));  // open: en
  Register #(.width(1)) register_3 (.D(and_6_out), .clk(CLK), .Q(mv), .clr(RST));  // open: en
  Register #(.width(1)) register_4 (.D(and_7_out), .clk(CLK), .Q(ldi), .clr(RST));  // open: en
  Register #(.width(1)) register_5 (.D(and_8_out), .clk(CLK), .Q(load), .clr(RST));  // open: en
  Register #(.width(1)) register_6 (.D(and_9_out), .clk(CLK), .Q(register_6_q), .clr(RST));  // open: en
  Register #(.width(1)) register_7 (.D(and_10_out), .clk(CLK), .Q(sub), .clr(RST));  // open: en
  Register #(.width(2)) register_8 (.D(instruction[7:6]), .clk(CLK), .Q(rd), .clr(RST));  // open: en
  Register #(.width(2)) register_9 (.D(instruction[5:4]), .clk(CLK), .Q(rs), .clr(RST));  // open: en
  and and_11 (JumpNegative, and_2_out, NegativeResult);
  D_Flip_Flop d_ff_1 (.D(1'b1), .clk(CLK), .Q(d_ff_1_q), .reset(RST));  // open: Qn, preset
  or or_1 (AS, register_6_q, sub);
  or or_2 (Operation, mv, load, ldi, AS);
  and and_12 (jmp, and_4_out, d_ff_1_q);

  assign jd = instruction[7:2];
endmodule

module regWE (
  input  [1:0] Rd,
  input  regWrite,
  output reg0,
  output reg1,
  output reg2,
  output reg3
);

  wire not_1_out, not_2_out;

  not not_1 (not_1_out, Rd[1]);
  not not_2 (not_2_out, Rd[0]);
  and and_1 (reg0, not_1_out, not_2_out, regWrite);
  and and_2 (reg1, Rd[0], not_1_out, regWrite);
  and and_3 (reg2, Rd[1], not_2_out, regWrite);
  and and_4 (reg3, Rd[1], Rd[0], regWrite);
endmodule

module programCounter (
  input  [5:0] JumpData,
  input  clk,
  input  JumpFlag,
  input  rst,
  input  JumpNegativeFlag,
  output [5:0] count,
  output Low,
  output High,
  output clkout
);

  wire or_1_out;
  wire [5:0] adder_1_out, multiplexer_1_out;

  Adder #(.width(6)) adder_1 (.a(count), .b(6'b000001), .out(adder_1_out));  // open: cin, cout
  or or_1 (or_1_out, JumpFlag, JumpNegativeFlag);
  Multiplexer #(.width(6)) multiplexer_1 (.in0(adder_1_out), .in1(JumpData), .out(multiplexer_1_out), .sel(or_1_out));
  Register #(.width(6)) register_1 (.D(multiplexer_1_out), .en(1'b1), .clk(clk), .Q(count), .clr(rst));

  assign clkout = clk;
  assign High = 1'b1;
  assign Low = 1'b0;
endmodule

module zeroOpt (
  input  a,
  input  b,
  output s,
  output cout
);

  wire nor_1_out;

  nor nor_1 (nor_1_out, a, b);
  and and_1 (cout, a, b);
  nor nor_2 (s, nor_1_out, cout);

  // Notes on the sheet:
  //   0
  //   0
  //   14 Transistors
  //   FA0
  //   Matthew Robson
  //   2.75
  //   1.75
endmodule

module oneOpt (
  input  a,
  input  b,
  output s,
  output cout
);

  wire nand_1_out;

  or or_1 (cout, a, b);
  nand nand_1 (nand_1_out, a, b);
  nand nand_2 (s, cout, nand_1_out);

  // Notes on the sheet:
  //   0
  //   0
  //   14 Transistors
  //   FA1
  //   Matthew Robson
  //   2.75
  //   1.75
endmodule

module FAopt1 (
  input  a,
  input  b,
  input  cin,
  output s,
  output cout
);

  wire nand_1_out, nand_2_out, nor_1_out, nor_2_out, nor_3_out, not_1_out, not_2_out;

  nor nor_1 (nor_1_out, a, b);
  nand nand_1 (nand_1_out, a, b);
  not not_1 (not_1_out, nand_1_out);
  nor nor_2 (nor_2_out, nor_1_out, not_1_out);
  nor nor_3 (nor_3_out, nor_2_out, cin);
  nand nand_2 (nand_2_out, nor_2_out, cin);
  not not_2 (not_2_out, nand_2_out);
  nand nand_3 (cout, nand_2_out, nand_1_out);
  nor nor_4 (s, nor_3_out, not_2_out);

  // Notes on the sheet:
  //   0
  //   0
  //   32 Transistors
  //   FAopt1 
  //   Matthew Robson
  //   if cin < 2.75 then 5.5 else 2.75 + cin
  //   if cin < 2.75 then 4.75 else 2 + cin
endmodule

module FAopt2 (
  input  a,
  input  b,
  input  cin,
  output s,
  output cout
);

  wire and_1_out, nand_1_out, nand_2_out, nand_3_out, nor_1_out, nor_2_out, nor_3_out, not_1_out;

  nor nor_1 (nor_1_out, a, b);
  nand nand_1 (nand_1_out, a, b);
  nand nand_2 (nand_2_out, b, cin);
  nand nand_3 (nand_3_out, cin, a);
  not not_1 (not_1_out, nand_1_out);
  nand nand_4 (cout, nand_1_out, nand_2_out, nand_3_out);
  nor nor_2 (nor_2_out, nor_1_out, not_1_out);
  nor nor_3 (nor_3_out, nor_2_out, cin);
  and and_1 (and_1_out, nor_2_out, cin);
  nor nor_4 (s, nor_3_out, and_1_out);

  // Notes on the sheet:
  //   0
  //   0
  //   42 Transistors
  //   FAopt2 
  //   Matthew Robson
  //   2.25 + cin
  //   if cin < 2.75 then 5.5 else 2.75 + cin 
endmodule

module rcAdder (
  input  [3:0] a,
  input  [3:0] b,
  output [3:0] _8_75,
  output _8
);

  wire faopt1_2_cout, faopt2_1_cout, zeroopt_1_cout;

  FAopt1 faopt1_1 (.a(b[3]), .b(a[3]), .cin(faopt1_2_cout), .s(_8_75[3]), .cout(_8));
  FAopt1 faopt1_2 (.a(a[2]), .b(b[2]), .cin(faopt2_1_cout), .s(_8_75[2]), .cout(faopt1_2_cout));
  FAopt2 faopt2_1 (.a(a[1]), .b(b[1]), .cin(zeroopt_1_cout), .s(_8_75[1]), .cout(faopt2_1_cout));
  zeroOpt zeroopt_1 (.a(b[0]), .b(a[0]), .s(_8_75[0]), .cout(zeroopt_1_cout));

  // Notes on the sheet:
  //   120 Transistors
  //   Matthew Robson
  //   rcAdder
  //   8
  //   6
  //   8.75
  //   6.75
  //   4
  //   5.5
  //   1.75
  //   2.75
endmodule

module fba0 (
  input  [3:0] a,
  input  [3:0] b,
  output [3:0] sum,
  output cout
);

  wire faopt1_2_cout, faopt2_1_cout, zeroopt_1_cout;

  FAopt1 faopt1_1 (.a(b[3]), .b(a[3]), .cin(faopt1_2_cout), .s(sum[3]), .cout(cout));
  FAopt1 faopt1_2 (.a(a[2]), .b(b[2]), .cin(faopt2_1_cout), .s(sum[2]), .cout(faopt1_2_cout));
  FAopt2 faopt2_1 (.a(a[1]), .b(b[1]), .cin(zeroopt_1_cout), .s(sum[1]), .cout(faopt2_1_cout));
  zeroOpt zeroopt_1 (.a(b[0]), .b(a[0]), .s(sum[0]), .cout(zeroopt_1_cout));

  // Notes on the sheet:
  //   Matthew Robson
  //   rcAdder
  //   8
  //   6
  //   8.75
  //   6.75
  //   4
  //   5.5
  //   8.75
  //   8
  //   1.75
  //   2.75
endmodule

module fba1 (
  input  [3:0] a,
  input  [3:0] b,
  output [3:0] sum,
  output cout
);

  wire faopt1_2_cout, faopt2_1_cout, oneopt_1_cout;

  FAopt1 faopt1_1 (.a(b[3]), .b(a[3]), .cin(faopt1_2_cout), .s(sum[3]), .cout(cout));
  FAopt1 faopt1_2 (.a(a[2]), .b(b[2]), .cin(faopt2_1_cout), .s(sum[2]), .cout(faopt1_2_cout));
  FAopt2 faopt2_1 (.a(a[1]), .b(b[1]), .cin(oneopt_1_cout), .s(sum[1]), .cout(faopt2_1_cout));
  oneOpt oneopt_1 (.a(a[0]), .b(b[0]), .s(sum[0]), .cout(oneopt_1_cout));

  // Notes on the sheet:
  //   Matthew Robson
  //   rcAdder
  //   8
  //   6
  //   8.75
  //   6.75
  //   4
  //   5.5
  //   8.75
  //   8
  //   1.75
  //   2.75
endmodule

module fba2 (
  input  cin,
  input  [3:0] a,
  input  [3:0] b,
  output [3:0] sum,
  output cout
);

  wire faopt1_2_cout, faopt2_1_cout, faopt2_2_cout;

  FAopt1 faopt1_1 (.a(b[3]), .b(a[3]), .cin(faopt1_2_cout), .s(sum[3]), .cout(cout));
  FAopt1 faopt1_2 (.a(a[2]), .b(b[2]), .cin(faopt2_1_cout), .s(sum[2]), .cout(faopt1_2_cout));
  FAopt2 faopt2_1 (.a(a[1]), .b(b[1]), .cin(faopt2_2_cout), .s(sum[1]), .cout(faopt2_1_cout));
  FAopt2 faopt2_2 (.a(a[0]), .b(b[0]), .cin(cin), .s(sum[0]), .cout(faopt2_2_cout));

  // Notes on the sheet:
  //   Matthew Robson
  //   rcAdder
  //   8.75
  //   8
endmodule

module rcAdderEight (
  input  [7:0] a,
  input  [7:0] b,
  output [7:0] _16_75,
  output _16
);

  wire faopt1_2_cout, faopt1_3_cout, faopt1_4_cout, faopt1_5_cout, faopt1_6_cout, faopt2_1_cout,
       zeroopt_1_cout;

  FAopt1 faopt1_1 (.a(b[7]), .b(a[7]), .cin(faopt1_2_cout), .s(_16_75[7]), .cout(_16));
  FAopt1 faopt1_2 (.a(a[6]), .b(b[6]), .cin(faopt1_3_cout), .s(_16_75[6]), .cout(faopt1_2_cout));
  FAopt1 faopt1_3 (.a(a[5]), .b(b[5]), .cin(faopt1_4_cout), .s(_16_75[5]), .cout(faopt1_3_cout));
  FAopt1 faopt1_4 (.a(a[4]), .b(b[4]), .cin(faopt1_5_cout), .s(_16_75[4]), .cout(faopt1_4_cout));
  FAopt1 faopt1_5 (.a(a[3]), .b(b[3]), .cin(faopt1_6_cout), .s(_16_75[3]), .cout(faopt1_5_cout));
  FAopt1 faopt1_6 (.a(a[2]), .b(b[2]), .cin(faopt2_1_cout), .s(_16_75[2]), .cout(faopt1_6_cout));
  FAopt2 faopt2_1 (.a(a[1]), .b(b[1]), .cin(zeroopt_1_cout), .s(_16_75[1]), .cout(faopt2_1_cout));
  zeroOpt zeroopt_1 (.a(b[0]), .b(a[0]), .s(_16_75[0]), .cout(zeroopt_1_cout));

  // Notes on the sheet:
  //   248 Transistors
  //   Matthew Robson
  //   rcAdder 8 bit
  //   16
  //   14
  //   16.75
  //   14.75
  //   12
  //   10
  //   12.75
  //   8
  //   10.75
  //   6
  //   8.75
  //   6.75
  //   4
  //   1.75
  //   4.75
  //   2.75
endmodule

module ebcsa0 (
  input  [7:0] a,
  input  [7:0] b,
  output [7:0] sum,
  output cout
);

  wire fba0_1_cout, fba0_2_cout, fba1_1_cout;
  wire [3:0] fba0_1_sum, fba1_1_sum;

  fba1 fba1_1 (.a(a[7:4]), .b(b[7:4]), .sum(fba1_1_sum), .cout(fba1_1_cout));
  mux2inlogic mux2inlogic_1 (.I0(fba0_1_cout), .I1(fba1_1_cout), .S(fba0_2_cout), .z(cout));
  fba0 fba0_1 (.a(a[7:4]), .b(b[7:4]), .sum(fba0_1_sum), .cout(fba0_1_cout));
  fbmux fbmux_1 (.in0(fba0_1_sum), .in1(fba1_1_sum), .sel(fba0_2_cout), .q(sum[7:4]));
  fba0 fba0_2 (.a(a[3:0]), .b(b[3:0]), .sum(sum[3:0]), .cout(fba0_2_cout));

  // Notes on the sheet:
  //   Matthew Robson
  //   8-Bit Carry Select Adder
  //   8
  //   8
  //   8.75
  //   8.75
  //   8
  //   z = max(sel+2.5, in0+1.75, in2+1.75)
  //   8.75
  //   10.5
  //   10.5
endmodule

module ebcsa1 (
  input  [7:0] a,
  input  [7:0] b,
  output [7:0] sum,
  output cout
);

  wire fba0_1_cout, fba1_1_cout, fba1_2_cout;
  wire [3:0] fba0_1_sum, fba1_1_sum;

  fba1 fba1_1 (.a(a[7:4]), .b(b[7:4]), .sum(fba1_1_sum), .cout(fba1_1_cout));
  mux2inlogic mux2inlogic_1 (.I0(fba0_1_cout), .I1(fba1_1_cout), .S(fba1_2_cout), .z(cout));
  fba0 fba0_1 (.a(a[7:4]), .b(b[7:4]), .sum(fba0_1_sum), .cout(fba0_1_cout));
  fbmux fbmux_1 (.in0(fba0_1_sum), .in1(fba1_1_sum), .sel(fba1_2_cout), .q(sum[7:4]));
  fba1 fba1_2 (.a(a[3:0]), .b(b[3:0]), .sum(sum[3:0]), .cout(fba1_2_cout));

  // Notes on the sheet:
  //   Matthew Robson
  //   8-Bit Carry Select Adder
  //   8
  //   8
  //   8.75
  //   8.75
  //   8
  //   z = max(sel+2.5, in0+1.75, in2+1.75)
  //   8.75
  //   10.5
  //   10.5
endmodule

module ebcsa2 (
  input  [7:0] a,
  input  [7:0] b,
  input  cin,
  output [7:0] sum,
  output cout
);

  wire fba0_1_cout, fba1_1_cout, fba2_1_cout;
  wire [3:0] fba0_1_sum, fba1_1_sum;

  fba1 fba1_1 (.a(a[7:4]), .b(b[7:4]), .sum(fba1_1_sum), .cout(fba1_1_cout));
  mux2inlogic mux2inlogic_1 (.I0(fba0_1_cout), .I1(fba1_1_cout), .S(fba2_1_cout), .z(cout));
  fba0 fba0_1 (.a(a[7:4]), .b(b[7:4]), .sum(fba0_1_sum), .cout(fba0_1_cout));
  fbmux fbmux_1 (.in0(fba0_1_sum), .in1(fba1_1_sum), .sel(fba2_1_cout), .q(sum[7:4]));
  fba2 fba2_1 (.cin(cin), .a(a[3:0]), .b(b[3:0]), .sum(sum[3:0]), .cout(fba2_1_cout));

  // Notes on the sheet:
  //   Matthew Robson
  //   8-Bit Carry Select Adder
  //   8
  //   8
  //   8.75
  //   8.75
  //   8
  //   z = max(sel+2.5, in0+1.75, in2+1.75)
  //   8.75
  //   10.5
  //   10.5
endmodule

module mux2inlogic (
  input  I0,
  input  I1,
  input  S,
  output z
);

  wire nand_1_out, nand_2_out, not_1_out;

  not not_1 (not_1_out, S);
  nand nand_1 (nand_1_out, not_1_out, I0);
  nand nand_2 (nand_2_out, I1, S);
  nand nand_3 (z, nand_1_out, nand_2_out);

  // Notes on the sheet:
  //   14 Transistors
  //   Two input Mux
  //   Matthew Robson
  //   z = max(S + 2.75, I0 + 2.75, I1 + 2)
endmodule

module mux4inlogic (
  input  I00,
  input  I01,
  input  I10,
  input  I11,
  input  S0,
  input  S1,
  output Four_input_Mux
);

  wire mux2inlogic_1_z, mux2inlogic_2_z;

  mux2inlogic mux2inlogic_1 (.I0(I00), .I1(I01), .S(S0), .z(mux2inlogic_1_z));
  mux2inlogic mux2inlogic_2 (.I0(I10), .I1(I11), .S(S0), .z(mux2inlogic_2_z));
  mux2inlogic mux2inlogic_3 (.I0(mux2inlogic_1_z), .I1(mux2inlogic_2_z), .S(S1), .z(Four_input_Mux));

  // Notes on the sheet:
  //   Matthew Robson
  //   42 Transistors
  //   z = max(S1 + 2.75, S0 + 4.75, in00 + 4, in01 + 4, in10 + 4, in11 + 4)
endmodule

module mx2i (
  input  in0,
  input  in1,
  input  sel,
  output z
);

  wire not_1_out, transmission_1_p4;

  not not_1 (not_1_out, sel);
  // Transmission_Gate transmission_1: pin names not known; wires that end beside it: in0, sel, not_1_out, transmission_1_p4
  // Transmission_Gate transmission_2: pin names not known; wires that end beside it: in1, not_1_out, sel, transmission_1_p4
  not not_2 (z, transmission_1_p4);

  // Notes on the sheet:
  //   8 Transistors
  //   mx2i
  //   Matthew Robson
  //   z = max(sel+1.75, in0+1, in2+1)
endmodule

module mux4trans (
  input  I00,
  input  I01,
  input  I10,
  input  I11,
  input  S1,
  input  S0,
  output Four_input_Mux
);

  wire mx2i_1_z, mx2i_2_z;

  mx2i mx2i_1 (.in0(I00), .in1(I01), .sel(S0), .z(mx2i_1_z));
  mx2i mx2i_2 (.in0(I10), .in1(I11), .sel(S0), .z(mx2i_2_z));
  mx2i mx2i_3 (.in0(mx2i_1_z), .in1(mx2i_2_z), .sel(S1), .z(Four_input_Mux));

  // Notes on the sheet:
  //   Matthew Robson
  //   32 Transistors
  //   z = max(S1 + 1.75, S0 + 2.75, in00 + 2, in01 + 2, in10 + 2, in11 + 2)
endmodule

module fbmux (
  input  [3:0] in0,
  input  [3:0] in1,
  input  sel,
  output [3:0] q
);

  wire mx2i_1_z, mx2i_2_z, mx2i_3_z, mx2i_4_z;

  mx2i mx2i_1 (.in0(in0[0]), .in1(in1[0]), .sel(sel), .z(mx2i_1_z));
  mx2i mx2i_2 (.in0(in0[1]), .in1(in1[1]), .sel(sel), .z(mx2i_2_z));
  mx2i mx2i_3 (.in0(in0[2]), .in1(in1[2]), .sel(sel), .z(mx2i_3_z));
  mx2i mx2i_4 (.in0(in0[3]), .in1(in1[3]), .sel(sel), .z(mx2i_4_z));
  not not_1 (q[0], mx2i_1_z);
  not not_2 (q[1], mx2i_2_z);
  not not_3 (q[2], mx2i_3_z);
  not not_4 (q[3], mx2i_4_z);

  // Notes on the sheet:
  //   z = max(sel+2.5, in0+1.75, in2+1.75)
endmodule

module ebmux (
  input  [7:0] in0,
  input  [7:0] in1,
  input  sel,
  output [7:0] q
);

  wire mx2i_1_z, mx2i_2_z, mx2i_3_z, mx2i_4_z, mx2i_5_z, mx2i_6_z, mx2i_7_z, mx2i_8_z;

  mx2i mx2i_1 (.in0(in0[0]), .in1(in1[0]), .sel(sel), .z(mx2i_1_z));
  mx2i mx2i_2 (.in0(in0[1]), .in1(in1[1]), .sel(sel), .z(mx2i_2_z));
  mx2i mx2i_3 (.in0(in0[2]), .in1(in1[2]), .sel(sel), .z(mx2i_3_z));
  mx2i mx2i_4 (.in0(in0[3]), .in1(in1[3]), .sel(sel), .z(mx2i_4_z));
  mx2i mx2i_5 (.in0(in0[4]), .in1(in1[4]), .sel(sel), .z(mx2i_5_z));
  mx2i mx2i_6 (.in0(in0[5]), .in1(in1[5]), .sel(sel), .z(mx2i_6_z));
  mx2i mx2i_7 (.in0(in0[6]), .in1(in1[6]), .sel(sel), .z(mx2i_7_z));
  mx2i mx2i_8 (.in0(in0[7]), .in1(in1[7]), .sel(sel), .z(mx2i_8_z));
  not not_1 (q[0], mx2i_1_z);
  not not_2 (q[1], mx2i_2_z);
  not not_3 (q[2], mx2i_3_z);
  not not_4 (q[3], mx2i_4_z);
  not not_5 (q[4], mx2i_5_z);
  not not_6 (q[5], mx2i_6_z);
  not not_7 (q[6], mx2i_7_z);
  not not_8 (q[7], mx2i_8_z);

  // Notes on the sheet:
  //   z = max(sel+2.5, in0+1.75, in2+1.75)
endmodule

module sbcsa (
  input  [15:0] a,
  input  [15:0] b,
  output [15:0] sum,
  output cout
);

  wire ebcsa0_1_cout, ebcsa0_2_cout, ebcsa1_1_cout;
  wire [7:0] ebcsa0_1_sum, ebcsa1_1_sum;

  ebcsa1 ebcsa1_1 (.a(b[15:8]), .b(a[15:8]), .sum(ebcsa1_1_sum), .cout(ebcsa1_1_cout));
  mux2inlogic mux2inlogic_1 (.I0(ebcsa0_1_cout), .I1(ebcsa1_1_cout), .S(ebcsa0_2_cout), .z(cout));
  ebcsa0 ebcsa0_1 (.a(b[15:8]), .b(a[15:8]), .sum(ebcsa0_1_sum), .cout(ebcsa0_1_cout));
  ebmux ebmux_1 (.in0(ebcsa0_1_sum), .in1(ebcsa1_1_sum), .sel(ebcsa0_2_cout), .q(sum[15:8]));
  ebcsa0 ebcsa0_2 (.a(b[7:0]), .b(a[7:0]), .sum(sum[7:0]), .cout(ebcsa0_2_cout));

  // Notes on the sheet:
  //   Matthew Robson
  //   10.5
  //   16-Bit Carry Select Adder
  //   10.5
  //   10.5
  //   10.5
  //   10.5
  //   z = max(sel+2.5, in0+1.75, in2+1.75)
  //   10.5
  //   13
  //   13
endmodule

module CLAC4SOP (
  input  c0,
  input  g0,
  input  g1,
  input  g2,
  input  g3,
  input  p0,
  input  p1,
  input  p2,
  input  p3,
  output c4
);

  wire and_1_out, and_2_out, and_3_out, and_4_out;

  and and_1 (and_1_out, g0, p1, p2, p3);
  and and_2 (and_2_out, g1, p2, p3);
  and and_3 (and_3_out, g2, p3);
  and and_4 (and_4_out, c0, p0, p1, p2, p3);
  or or_1 (c4, g3, and_1_out, and_2_out, and_3_out, and_4_out);
endmodule

module label1 (
  input  c0,
  input  g0,
  input  g1,
  input  g2,
  input  g3,
  input  p0,
  input  p1,
  input  p2,
  input  p3,
  output c4
);

  wire and_1_out, and_2_out, and_3_out, and_4_out;

  and and_1 (and_1_out, g0, p1, p2, p3);
  and and_2 (and_2_out, g1, p2, p3);
  and and_3 (and_3_out, g2, p3);
  and and_4 (and_4_out, c0, p0, p1, p2, p3);
  or or_1 (c4, g3, and_1_out, and_2_out, and_3_out, and_4_out);

  // Notes on the sheet:
  //   Matthew Robson
  //   Carry Look Ahead Adder C4
endmodule

module CLAC4OP (
  input  c0,
  input  g0,
  input  g1,
  input  g2,
  input  g3,
  input  p0,
  input  p1,
  input  p2,
  input  p3,
  output c4
);

  wire nand_1_out, nand_2_out, nand_3_out, nand_4_out, nand_5_out, nand_6_out, nor_1_out, nor_2_out,
       nor_3_out, nor_4_out, not_1_out, not_2_out;

  nand nand_1 (nand_1_out, g0, p1);
  nand nand_2 (nand_2_out, p3, p2);
  not not_1 (not_1_out, nand_3_out);
  nand nand_3 (nand_3_out, g1, p2, p3);
  nand nand_4 (nand_4_out, g2, p3);
  not not_2 (not_2_out, nand_4_out);
  nand nand_5 (nand_5_out, c0, p0, p1);
  nand nand_6 (nand_6_out, p3, p2);
  nor nor_1 (nor_1_out, nand_1_out, nand_2_out);
  nor nor_2 (nor_2_out, nand_5_out, nand_6_out);
  nor nor_3 (nor_3_out, g3, nor_1_out, not_1_out);
  nand nand_7 (c4, nor_3_out, nor_4_out);
  nor nor_4 (nor_4_out, not_2_out, nor_2_out);
endmodule

module label2 (
  input  c0,
  input  g0,
  input  g1,
  input  g2,
  input  g3,
  input  p0,
  input  p1,
  input  p2,
  input  p3,
  output c4
);

  wire nand_1_out, nand_2_out, nand_3_out, nand_4_out, nand_5_out, nand_6_out, nor_1_out, nor_2_out,
       nor_3_out, nor_4_out, not_1_out, not_2_out;

  nand nand_1 (nand_1_out, p1, g0);
  nand nand_2 (nand_2_out, p3, p2);
  nand nand_3 (nand_3_out, g1, p2, p3);
  not not_1 (not_1_out, nand_3_out);
  nand nand_4 (nand_4_out, g2, p3);
  not not_2 (not_2_out, nand_4_out);
  nand nand_5 (nand_5_out, c0, p0, p1);
  nand nand_6 (nand_6_out, p3, p2);
  nor nor_1 (nor_1_out, nand_1_out, nand_2_out);
  nor nor_2 (nor_2_out, nand_5_out, nand_6_out);
  nor nor_3 (nor_3_out, nor_1_out, g3, not_1_out);
  nor nor_4 (nor_4_out, nor_2_out, not_2_out);
  nand nand_7 (c4, nor_3_out, nor_4_out);

  // Notes on the sheet:
  //   1.25
  //   2.25
  //   3.25
  //   4.25
  //   Matthew Robson
  //   Carry Look Ahead Adder Optimized
endmodule

module CLAC4AOI21OP (
  input  c0,
  input  g0,
  input  g1,
  input  g2,
  input  g3,
  input  p0,
  input  p1,
  input  p2,
  input  p3,
  output c4
);

  wire and_1_out, and_2_out, and_3_out, nand_1_out, nand_2_out, nand_3_out, nand_4_out, nand_5_out,
       nor_1_out, nor_2_out, nor_3_out, nor_4_out, nor_5_out;

  nand nand_1 (nand_1_out, g0, p1);
  nand nand_2 (nand_2_out, p2, p3);
  and and_1 (and_1_out, p3, g1, p2);
  nor nor_1 (nor_1_out, nand_2_out, nand_1_out);
  and and_2 (and_2_out, g2, p3);
  nor nor_2 (nor_2_out, nor_1_out, and_1_out);
  nor nor_3 (nor_3_out, and_2_out, g3);
  nand nand_3 (nand_3_out, p0, p1);
  nand nand_4 (nand_4_out, p2, p3);
  nand nand_5 (nand_5_out, nor_2_out, nor_3_out);
  and and_3 (and_3_out, c0, nor_4_out);
  nor nor_4 (nor_4_out, nand_3_out, nand_4_out);
  nor nor_5 (nor_5_out, and_3_out, nand_5_out);
  not not_1 (c4, nor_5_out);
endmodule

module CLAC4AIO21trans (
  input  c0,
  input  g0,
  input  g1,
  input  g2,
  input  g3,
  input  p0,
  input  p1,
  input  p2,
  input  p3,
  output c4
);

  wire and_1_out, and_2_out, aoi21trans_1_c4, nand_1_out, nand_2_out, nand_3_out, nand_4_out, nand_5_out,
       nor_1_out, nor_2_out, nor_3_out, nor_4_out;

  nand nand_1 (nand_1_out, g0, p1);
  nand nand_2 (nand_2_out, p2, p3);
  and and_1 (and_1_out, p3, g1, p2);
  nor nor_1 (nor_1_out, nand_2_out, nand_1_out);
  and and_2 (and_2_out, g2, p3);
  nor nor_2 (nor_2_out, nor_1_out, and_1_out);
  nor nor_3 (nor_3_out, and_2_out, g3);
  nand nand_3 (nand_3_out, p0, p1);
  nand nand_4 (nand_4_out, p2, p3);
  nand nand_5 (nand_5_out, nor_2_out, nor_3_out);
  nor nor_4 (nor_4_out, nand_3_out, nand_4_out);
  not not_1 (c4, aoi21trans_1_c4);
  AOI21trans aoi21trans_1 (.c0(c0), .y(nor_4_out), .x(nand_5_out), .c4(aoi21trans_1_c4));
endmodule

module label3 (
  input  c0,
  input  g0,
  input  g1,
  input  g2,
  input  g3,
  input  p0,
  input  p1,
  input  p2,
  input  p3,
  output c4
);

  wire and_1_out, and_2_out, aoi21trans_1_c4, nand_1_out, nand_2_out, nand_3_out, nand_4_out, nand_5_out,
       nor_1_out, nor_2_out, nor_3_out, nor_4_out;

  nand nand_1 (nand_1_out, g0, p1);
  nand nand_2 (nand_2_out, p2, p3);
  and and_1 (and_1_out, p3, g1, p2);
  nor nor_1 (nor_1_out, nand_2_out, nand_1_out);
  and and_2 (and_2_out, g2, p3);
  nor nor_2 (nor_2_out, nor_1_out, and_1_out);
  nor nor_3 (nor_3_out, and_2_out, g3);
  nand nand_3 (nand_3_out, p0, p1);
  nand nand_4 (nand_4_out, p2, p3);
  nand nand_5 (nand_5_out, nor_2_out, nor_3_out);
  nor nor_4 (nor_4_out, nand_3_out, nand_4_out);
  not not_1 (c4, aoi21trans_1_c4);
  AOI21trans aoi21trans_1 (.c0(c0), .y(nor_4_out), .x(nand_5_out), .c4(aoi21trans_1_c4));

  // Notes on the sheet:
  //   1
  //   2
  //   3
  //   4
  //   5.25
  //   6
endmodule

module AddSub (
  input  [15:0] a,
  input  [15:0] b,
  input  opp,
  output ovfl,
  output [15:0] z
);

  wire not_2_out, xor_1_out, xor_2_out;
  wire [15:0] multiplexer_1_out, not_1_out;

  Multiplexer #(.width(16)) multiplexer_1 (.in0(b), .in1(not_1_out), .out(multiplexer_1_out), .sel(opp));
  assign not_1_out = ~b;  // NOT_Gate not_1, 16 bits wide
  Adder #(.width(16)) adder_1 (.a(a), .b(multiplexer_1_out), .out(z), .cin(opp));  // open: cout
  xor xor_1 (xor_1_out, a[15], multiplexer_1_out[15]);
  xor xor_2 (xor_2_out, multiplexer_1_out[15], z[15]);
  finalAdder finaladder_1 ();  // open: a, b, opp, sum, ovfl
  not not_2 (not_2_out, xor_1_out);
  and and_1 (ovfl, not_2_out, xor_2_out);

  // Notes on the sheet:
  //   32767
endmodule

module finalAdder (
  input  [15:0] a,
  input  [15:0] b,
  input  opp,
  output ovfl,
  output [15:0] sum
);

  wire ebcsa2_1_cout, not_2_out, xor_1_out, xor_2_out;
  wire [7:0] ebcsa0_1_sum, ebcsa1_1_sum, multiplexer_1_out, multiplexer_1_out_2;
  wire [15:0] not_1_out;

  Multiplexer #(.width(16)) multiplexer_1 (
    .in0(b), .in1(not_1_out), .out({multiplexer_1_out_2, multiplexer_1_out}), .sel(opp));
  assign not_1_out = ~b;  // NOT_Gate not_1, 16 bits wide
  ebcsa1 ebcsa1_1 (.a(multiplexer_1_out_2), .b(a[15:8]), .sum(ebcsa1_1_sum));  // open: cout
  ebcsa0 ebcsa0_1 (.a(multiplexer_1_out_2), .b(a[15:8]), .sum(ebcsa0_1_sum));  // open: cout
  ebmux ebmux_1 (.in0(ebcsa0_1_sum), .in1(ebcsa1_1_sum), .sel(ebcsa2_1_cout), .q(sum[15:8]));
  ebcsa2 ebcsa2_1 (.cin(opp), .a(multiplexer_1_out), .b(a[7:0]), .sum(sum[7:0]), .cout(ebcsa2_1_cout));
  xor xor_1 (xor_1_out, a[15], multiplexer_1_out_2[7]);
  not not_2 (not_2_out, xor_1_out);
  xor xor_2 (xor_2_out, multiplexer_1_out_2[7], sum[15]);
  and and_1 (ovfl, not_2_out, xor_2_out);

  // Notes on the sheet:
  //   Matthew Robson
  //   16-Bit Carry Select Adder
endmodule

module overflowExtra (
  input  op,
  input  a3,
  input  b3,
  input  r3,
  output ovfl
);

  wire and_1_out, xor_1_out, xor_2_out;

  xor xor_1 (xor_1_out, a3, b3);
  xor xor_2 (xor_2_out, b3, r3);
  and and_1 (and_1_out, op, xor_1_out);
  and and_2 (ovfl, and_1_out, xor_2_out);
endmodule

module AOI21logic (
  input  c0,
  input  y,
  input  x,
  output c4
);

  wire and_1_out;

  and and_1 (and_1_out, c0, y);
  nor nor_1 (c4, and_1_out, x);
endmodule

module AOI21trans (
  input  c0,
  input  y,
  input  x,
  output c4
);

  wire transistor_1_out, transistor_6_out;

  Transistor transistor_1 (.in(1'b1), .out(transistor_1_out), .gate(y));
  Transistor transistor_2 (.in(1'b1), .out(transistor_1_out), .gate(c0));
  Transistor transistor_3 (.in(transistor_1_out), .out(c4), .gate(x));
  Transistor #(.\type ("n")) transistor_4 (.in(transistor_6_out), .out(c4), .gate(y));
  Transistor #(.\type ("n")) transistor_5 (.in(1'b0), .out(c4), .gate(transistor_6_out));
  Transistor #(.\type ("n")) transistor_6 (.in(1'b0), .out(transistor_6_out), .gate(c0));
endmodule
